// Logisim project Project gates.circ as structural Verilog: 1 circuit, main circuit main
module main (
  input  A,
  input  C,
  input  D,
  input  E,
  input  B,
  input  P,
  input  Z
);

  wire AND_2_out, AND_3_out, AND_out, not_1_out, OR_out;

  and AND (AND_out, A, C, D, E);
  not not_1 (not_1_out, AND_out);
  or OR (OR_out, AND_out, P);
  and AND_2 (AND_2_out, not_1_out, E);
  LED led_1 (.in(AND_out));
  LED led_2 (.in(AND_2_out));
  and AND_3 (AND_3_out, OR_out, Z);
  LED led_3 (.in(AND_3_out));

  // Notes on the sheet:
  //   NOT
  //   U (Unlock)
  //   Green LED/ LOCK
  //   W (Denied)
  //   Red LED/ Buzzer
  //   L (Zone Power)
  //   Zone Loads
endmodule
